// Logisim project 29-BIT-BOOTHS-MULTIPLYER.circ as structural Verilog: 16 circuits, main circuit ALU
module ALU (
  input  [1:0] Control,
  input  [28:0] in_2,
  input  [28:0] in_3,
  output [28:0] out_4,
  output [3:0] Flags
);

  wire zero_check_1_output;
  wire [28:0] n29bit_adder_1_out_4, n29bit_and_1_out_3, n29bit_or_1_out_3;

  _29BIT_AND u_29bit_and_1 (.in_1(in_2), .in_2(in_3), .out_3(n29bit_and_1_out_3));
  _29BIT_OR u_29bit_or_1 (.in_1(in_3), .in_2(in_2), .out_3(n29bit_or_1_out_3));
  _29BIT_ADDER u_29bit_adder_1 (
    .in_1(Control[0]), .in_2(in_2), .in_3(in_3), .out_4(n29bit_adder_1_out_4), .out_5(Flags[1]),
    .out_6(Flags[0]));
  _4X1_MUX u_4x1_mux_1 (
    .in_1(Control), .in_2(n29bit_and_1_out_3), .in_3(n29bit_or_1_out_3), .in_4(n29bit_adder_1_out_4),
    .in_5(n29bit_adder_1_out_4), .out_6(out_4));
  Negative_Check negative_check_1 (.in_1(out_4), .Output(Flags[3]));
  Zero_Check zero_check_1 (.in_1(out_4), .Output(zero_check_1_output));
  not not_1 (Flags[2], zero_check_1_output);

  // Other names for the same wires on the sheet: Overflow = Flags[0]; Carry = Flags[1]; Zero = Flags[2];
  //   Negative = Flags[3]

  // Notes on the sheet:
  //   1 0 - Adder
  //   1 1 - Subtractor
  //   0 0 - AND
  //   0 1 - OR
  //   A
  //   B
  //   Output
  //   Negative- Zero-Carry-Overflow
  //   Roll - 2207006
endmodule

// AND
module _29BIT_AND (
  input  [28:0] in_1,
  input  [28:0] in_2,
  output [28:0] out_3
);

  assign out_3 = in_1 & in_2;  // AND_Gate and_1, 29 bits wide

  // Notes on the sheet:
  //   A
  //   B
  //   A & B
endmodule

// OR
module _29BIT_OR (
  input  [28:0] in_1,
  input  [28:0] in_2,
  output [28:0] out_3
);

  assign out_3 = in_1 | in_2;  // OR_Gate or_1, 29 bits wide

  // Notes on the sheet:
  //   A
  //   B
  //   A | B
endmodule

// 4bit CLA
module _4BIT_CLA (
  input  Cin,
  input  [3:0] in_2,
  input  [3:0] in_3,
  output C1,
  output C2,
  output C3,
  output C4
);

  wire and_1_out, and_2_out, and_3_out, and_4_out, and_5_out, and_6_out, and_7_out, and_8_out, and_9_out,
       and_10_out, and_11_out, and_12_out, and_13_out, and_14_out, xor_1_out, xor_2_out, xor_3_out, xor_4_out;

  xor xor_1 (xor_1_out, in_2[0], in_3[0]);
  xor xor_2 (xor_2_out, in_2[1], in_3[1]);
  xor xor_3 (xor_3_out, in_2[2], in_3[2]);
  xor xor_4 (xor_4_out, in_2[3], in_3[3]);
  and and_1 (and_1_out, in_2[0], in_3[0]);
  and and_2 (and_2_out, in_2[1], in_3[1]);
  and and_3 (and_3_out, in_2[2], in_3[2]);
  and and_4 (and_4_out, in_2[3], in_3[3]);
  and and_5 (and_5_out, Cin, xor_1_out);
  and and_6 (and_6_out, Cin, xor_1_out, xor_2_out);
  and and_7 (and_7_out, xor_2_out, and_1_out);
  and and_8 (and_8_out, xor_3_out, xor_2_out, xor_1_out, Cin);
  and and_9 (and_9_out, and_1_out, xor_2_out, xor_3_out);
  and and_10 (and_10_out, xor_3_out, and_2_out);
  and and_11 (and_11_out, xor_4_out, and_3_out);
  and and_12 (and_12_out, xor_4_out, xor_3_out, and_2_out);
  and and_13 (and_13_out, xor_4_out, xor_3_out, xor_2_out, and_1_out);
  and and_14 (and_14_out, xor_4_out, xor_3_out, xor_2_out, xor_1_out, Cin);
  or or_1 (C1, and_5_out, and_1_out);
  or or_2 (C2, and_6_out, and_7_out, and_2_out);
  or or_3 (C3, and_8_out, and_9_out, and_10_out, and_3_out);
  or or_4 (C4, and_14_out, and_13_out, and_12_out, and_11_out, and_4_out);

  // Notes on the sheet:
  //   A
  //   B
endmodule

module _4X1_MUX (
  input  [1:0] in_1,
  input  [28:0] in_2,
  input  [28:0] in_3,
  input  [28:0] in_4,
  input  [28:0] in_5,
  output [28:0] out_6
);

  wire [28:0] and_1_out, and_2_out, and_3_out, and_4_out, bit_extender_1_out, bit_extender_2_out, not_1_out,
       not_2_out, not_3_out, not_4_out;

  assign bit_extender_1_out = {{28{in_1[0]}}, in_1[0]};  // Bit_Extender bit_extender_1
  assign bit_extender_2_out = {{28{in_1[1]}}, in_1[1]};  // Bit_Extender bit_extender_2
  assign not_1_out = ~bit_extender_1_out;  // NOT_Gate not_1, 29 bits wide
  assign not_2_out = ~bit_extender_2_out;  // NOT_Gate not_2, 29 bits wide
  assign not_3_out = ~bit_extender_2_out;  // NOT_Gate not_3, 29 bits wide
  assign not_4_out = ~bit_extender_1_out;  // NOT_Gate not_4, 29 bits wide
  assign and_1_out = not_1_out & not_2_out & in_2;  // AND_Gate and_1, 29 bits wide
  assign and_2_out = bit_extender_1_out & not_3_out & in_3;  // AND_Gate and_2, 29 bits wide
  assign and_3_out = not_4_out & bit_extender_2_out & in_4;  // AND_Gate and_3, 29 bits wide
  assign and_4_out = bit_extender_1_out & bit_extender_2_out & in_5;  // AND_Gate and_4, 29 bits wide
  assign out_6 = and_1_out | and_2_out | and_3_out | and_4_out;  // OR_Gate or_1, 29 bits wide
endmodule

// 1bit CLA
module _1BIT_CLA (
  input  Cin,
  input  A,
  input  B,
  output Cout
);

  wire and_1_out, and_2_out, xor_1_out;

  and and_1 (and_1_out, A, B);
  xor xor_1 (xor_1_out, A, B);
  and and_2 (and_2_out, xor_1_out, Cin);
  or or_1 (Cout, and_1_out, and_2_out);
endmodule

// Adder
module FULLADDER (
  input  Cin,
  input  A,
  input  B,
  output Sum,
  output Carry
);

  wire and_1_out, and_2_out, xor_1_out;

  xor xor_1 (xor_1_out, A, B);
  and and_1 (and_1_out, B, A);
  xor xor_2 (Sum, Cin, xor_1_out);
  and and_2 (and_2_out, Cin, xor_1_out);
  or or_1 (Carry, and_2_out, and_1_out);
endmodule

module _29BIT_CLA (
  input  Cin,
  input  [28:0] in_2,
  input  [28:0] in_3,
  output [28:0] out_4
);

  _4BIT_CLA u_4bit_cla_1 (
    .Cin(Cin), .in_2(in_2[3:0]), .in_3(in_3[3:0]), .C1(out_4[0]), .C2(out_4[1]), .C3(out_4[2]), .C4(out_4[3]));
  _4BIT_CLA u_4bit_cla_2 (
    .Cin(out_4[3]), .in_2(in_2[7:4]), .in_3(in_3[7:4]), .C1(out_4[4]), .C2(out_4[5]), .C3(out_4[6]),
    .C4(out_4[7]));
  _4BIT_CLA u_4bit_cla_3 (
    .Cin(out_4[7]), .in_2(in_2[11:8]), .in_3(in_3[11:8]), .C1(out_4[8]), .C2(out_4[9]), .C3(out_4[10]),
    .C4(out_4[11]));
  _4BIT_CLA u_4bit_cla_4 (
    .Cin(out_4[11]), .in_2(in_2[15:12]), .in_3(in_3[15:12]), .C1(out_4[12]), .C2(out_4[13]), .C3(out_4[14]),
    .C4(out_4[15]));
  _4BIT_CLA u_4bit_cla_5 (
    .Cin(out_4[15]), .in_2(in_2[19:16]), .in_3(in_3[19:16]), .C1(out_4[16]), .C2(out_4[17]), .C3(out_4[18]),
    .C4(out_4[19]));
  _4BIT_CLA u_4bit_cla_6 (
    .Cin(out_4[19]), .in_2(in_2[23:20]), .in_3(in_3[23:20]), .C1(out_4[20]), .C2(out_4[21]), .C3(out_4[22]),
    .C4(out_4[23]));
  _4BIT_CLA u_4bit_cla_7 (
    .Cin(out_4[23]), .in_2(in_2[27:24]), .in_3(in_3[27:24]), .C1(out_4[24]), .C2(out_4[25]), .C3(out_4[26]),
    .C4(out_4[27]));
  _1BIT_CLA u_1bit_cla_1 (.Cin(out_4[27]), .A(in_2[28]), .B(in_3[28]), .Cout(out_4[28]));

  // Notes on the sheet:
  //   A
  //   B
  //   Cout
endmodule

module _4BIT_ADDER (
  input  [3:0] in_1,
  input  [3:0] in_2,
  input  [3:0] in_3,
  output [3:0] out_4
);

  FULLADDER fulladder_1 (.Cin(in_1[0]), .A(in_2[0]), .B(in_3[0]), .Sum(out_4[0]));  // open: Carry
  FULLADDER fulladder_2 (.Cin(in_1[1]), .A(in_2[1]), .B(in_3[1]), .Sum(out_4[1]));  // open: Carry
  FULLADDER fulladder_3 (.Cin(in_1[2]), .A(in_2[2]), .B(in_3[2]), .Sum(out_4[2]));  // open: Carry
  FULLADDER fulladder_4 (.Cin(in_1[3]), .A(in_2[3]), .B(in_3[3]), .Sum(out_4[3]));  // open: Carry
endmodule

// Zero
module Zero_Check (
  input  [28:0] in_1,
  output Output
);

  or or_1 (Output, in_1[0], in_1[1], in_1[2], in_1[3], in_1[4], in_1[5], in_1[6], in_1[7], in_1[8], in_1[9], in_1[10], in_1[11], in_1[12], in_1[13], in_1[14], in_1[15], in_1[16], in_1[17], in_1[18], in_1[19], in_1[20], in_1[21], in_1[22], in_1[23], in_1[24], in_1[25], in_1[26], in_1[27], in_1[28]);

  // Notes on the sheet:
  //   Input
endmodule

// Neg
module Negative_Check (
  input  [28:0] in_1,
  output Output
);


  assign Output = in_1[28];

  // Notes on the sheet:
  //   Input
endmodule

// Add-Sub
module _29BIT_ADDER (
  input  in_1,
  input  [28:0] in_2,
  input  [28:0] in_3,
  output [28:0] out_4,
  output out_5,
  output out_6
);

  wire and_1_out, and_2_out, not_1_out, not_2_out, not_3_out;
  wire [27:0] n29bit_cla_1_out_4;
  wire [28:0] bit_extender_1_out, xor_1_out;

  assign bit_extender_1_out = {{28{in_1}}, in_1};  // Bit_Extender bit_extender_1
  _29BIT_CLA u_29bit_cla_1 (.Cin(in_1), .in_2(in_2), .in_3(xor_1_out), .out_4({out_5, n29bit_cla_1_out_4}));
  assign xor_1_out = in_3 ^ bit_extender_1_out;  // XOR_Gate xor_1, 29 bits wide
  _4BIT_ADDER u_4bit_adder_1 (
    .in_1({n29bit_cla_1_out_4[2:0], in_1}), .in_2(in_2[3:0]), .in_3(xor_1_out[3:0]), .out_4(out_4[3:0]));
  _4BIT_ADDER u_4bit_adder_2 (
    .in_1(n29bit_cla_1_out_4[6:3]), .in_2(in_2[7:4]), .in_3(xor_1_out[7:4]), .out_4(out_4[7:4]));
  _4BIT_ADDER u_4bit_adder_3 (
    .in_1(n29bit_cla_1_out_4[10:7]), .in_2(in_2[11:8]), .in_3(xor_1_out[11:8]), .out_4(out_4[11:8]));
  _4BIT_ADDER u_4bit_adder_4 (
    .in_1(n29bit_cla_1_out_4[14:11]), .in_2(in_2[15:12]), .in_3(xor_1_out[15:12]), .out_4(out_4[15:12]));
  _4BIT_ADDER u_4bit_adder_5 (
    .in_1(n29bit_cla_1_out_4[18:15]), .in_2(in_2[19:16]), .in_3(xor_1_out[19:16]), .out_4(out_4[19:16]));
  _4BIT_ADDER u_4bit_adder_6 (
    .in_1(n29bit_cla_1_out_4[22:19]), .in_2(in_2[23:20]), .in_3(xor_1_out[23:20]), .out_4(out_4[23:20]));
  _4BIT_ADDER u_4bit_adder_7 (
    .in_1(n29bit_cla_1_out_4[26:23]), .in_2(in_2[27:24]), .in_3(xor_1_out[27:24]), .out_4(out_4[27:24]));
  FULLADDER fulladder_1 (
    .Cin(n29bit_cla_1_out_4[27]), .A(in_2[28]), .B(xor_1_out[28]), .Sum(out_4[28]));  // open: Carry
  not not_1 (not_1_out, in_2[28]);
  not not_2 (not_2_out, xor_1_out[28]);
  and and_1 (and_1_out, not_1_out, not_2_out, out_4[28]);
  not not_3 (not_3_out, out_4[28]);
  and and_2 (and_2_out, not_3_out, in_2[28], xor_1_out[28]);
  or or_1 (out_6, and_1_out, and_2_out);

  // Notes on the sheet:
  //   A
  //   B
endmodule

module COUNTER (
  input  [1:0] Q,
  input  [2:0] T,
  input  C,
  output DA,
  output DB,
  output DC
);

  wire and_1_out, and_2_out, and_3_out, and_4_out, and_5_out, or_4_out, or_5_out, Q0, Q1, Q2, Q3, T0, T1, T2,
       T3, T4, T5, T6, T7;

  Decoder #(.select(3), .enable("false")) decoder_1 (
    .out0(T0), .out1(T1), .out2(T2), .out3(T3), .out4(T4), .out5(T5), .out6(T6), .out7(T7), .sel(T));
  or or_1 (DA, T0, and_4_out, T3, T4, and_5_out, T7);
  or or_2 (DB, T1, and_1_out, T5, T6, T6, T7);
  or or_3 (DC, T5, and_2_out, T3, T4, and_3_out, T7);
  Decoder #(.select(2), .enable("false")) decoder_2 (.out0(Q0), .out1(Q1), .out2(Q2), .out3(Q3), .sel(Q));
  and and_1 (and_1_out, T2, Q2);
  and and_2 (and_2_out, T2, or_4_out);
  and and_3 (and_3_out, T6, C);
  and and_4 (and_4_out, T2, or_5_out);
  and and_5 (and_5_out, T6, C);
  or or_4 (or_4_out, Q0, Q1, Q3);
  or or_5 (or_5_out, Q0, Q2, Q3);
endmodule

module CONTROLLER_CIRCUIT (
  input  Clk,
  input  Reset,
  input  Q0,
  input  Q_1,
  input  [4:0] Count,
  output Cl__A__Q_1,
  output LOad__M__Q__Cnt,
  output Load_A,
  output C0,
  output C1,
  output Shr,
  output Dec_Cnt
);

  wire counter_1_da, counter_1_db, counter_1_dc, nor_1_out, T0, T2, T4, T6, T7;
  wire [2:0] T;

  nor nor_1 (nor_1_out, Count[2], Count[3], Count[0], Count[1], Count[4]);
  Decoder #(.select(3), .enable("false")) decoder_1 (
    .out0(T0), .out1(Cl__A__Q_1), .out2(T2), .out3(C0), .out4(T4), .out5(Dec_Cnt), .out6(T6), .out7(T7),
    .sel(T));
  COUNTER counter_1 (.Q({Q0, Q_1}), .T(T), .C(nor_1_out), .DA(counter_1_da), .DB(counter_1_db), .DC(counter_1_dc));
  or or_1 (Load_A, C0, T4);
  or or_2 (C1, T4, C0);
  D_Flip_Flop d_ff_1 (.clk(Clk), .D(counter_1_da), .Q(T[0]), .reset(Reset));  // open: Qn, preset, en
  D_Flip_Flop d_ff_2 (.clk(Clk), .D(counter_1_db), .Q(T[1]), .reset(Reset));  // open: Qn, preset, en
  D_Flip_Flop d_ff_3 (.clk(Clk), .D(counter_1_dc), .Q(T[2]), .reset(Reset));  // open: Qn, preset, en

  assign LOad__M__Q__Cnt = Cl__A__Q_1;
  assign Shr = Dec_Cnt;

  // Other names for the same wires on the sheet: T1 = Cl__A__Q_1; T3 = C0; T5 = Dec_Cnt
endmodule

module _29BIT_2_S_COMPLEMENT (
  input  [28:0] Inp,
  output [28:0] out
);

  wire [27:0] not_1_out;
  wire [28:0] alu_1_out_4;

  not not_1 (not_1_out[0], Inp[0]);
  not not_2 (not_1_out[1], Inp[1]);
  not not_3 (not_1_out[2], Inp[2]);
  not not_4 (not_1_out[3], Inp[3]);
  not not_5 (not_1_out[4], Inp[4]);
  not not_6 (not_1_out[5], Inp[5]);
  not not_7 (not_1_out[6], Inp[6]);
  not not_8 (not_1_out[7], Inp[7]);
  not not_9 (not_1_out[8], Inp[8]);
  not not_10 (not_1_out[9], Inp[9]);
  not not_11 (not_1_out[10], Inp[10]);
  not not_12 (not_1_out[11], Inp[11]);
  not not_13 (not_1_out[12], Inp[12]);
  not not_14 (not_1_out[13], Inp[13]);
  not not_15 (not_1_out[14], Inp[14]);
  not not_16 (not_1_out[15], Inp[15]);
  not not_17 (not_1_out[16], Inp[16]);
  not not_18 (not_1_out[17], Inp[17]);
  not not_19 (not_1_out[18], Inp[18]);
  not not_20 (not_1_out[19], Inp[19]);
  not not_21 (not_1_out[20], Inp[20]);
  not not_22 (not_1_out[21], Inp[21]);
  not not_23 (not_1_out[22], Inp[22]);
  not not_24 (not_1_out[23], Inp[23]);
  not not_25 (not_1_out[24], Inp[24]);
  not not_26 (not_1_out[25], Inp[25]);
  not not_27 (not_1_out[26], Inp[26]);
  not not_28 (not_1_out[27], Inp[27]);
  ALU alu_1 (.Control(2'b10), .in_2({Inp[28], not_1_out}), .in_3(29'h1), .out_4(alu_1_out_4));  // open: Flags
  Multiplexer #(.width(29), .enable("false")) multiplexer_1 (.in0(Inp), .in1(alu_1_out_4), .out(out), .sel(Inp[28]));
endmodule

module BOOTH_S_MULTIPLYER (
  input  [28:0] in_1,
  input  [28:0] in_2,
  input  in_3,
  output [28:0] M29_57,
  output [28:0] M0_28
);

  wire clock_1_out, controller_circuit_1_cl__a__q_1, controller_circuit_1_dec_cnt,
       controller_circuit_1_load__m__q__cnt, controller_circuit_1_load_a, controller_circuit_1_shr, or_1_out,
       shift_register_1_out, shift_register_3_out, shift_register_4_q0;
  wire [1:0] controller_circuit_1_c0;
  wire [4:0] counter_1_q;
  wire [28:0] alu_1_out_4, n29bit_2_s_complement_1_out, n29bit_2_s_complement_2_out, shift_register_2_q28;

  CONTROLLER_CIRCUIT controller_circuit_1 (
    .Clk(clock_1_out), .Reset(in_3), .Q0(M0_28[0]), .Q_1(shift_register_4_q0), .Count(counter_1_q),
    .Cl__A__Q_1(controller_circuit_1_cl__a__q_1), .LOad__M__Q__Cnt(controller_circuit_1_load__m__q__cnt),
    .Load_A(controller_circuit_1_load_a), .C0(controller_circuit_1_c0[0]), .C1(controller_circuit_1_c0[1]),
    .Shr(controller_circuit_1_shr), .Dec_Cnt(controller_circuit_1_dec_cnt));
  Clock clock_1 (.out(clock_1_out));
  or or_1 (or_1_out, controller_circuit_1_dec_cnt, controller_circuit_1_load__m__q__cnt);
  Counter #(.width(5), .max('h1d)) counter_1 (
    .load(or_1_out), .D(5'b11101), .count(controller_circuit_1_dec_cnt), .Q(counter_1_q), .clk(clock_1_out));  // open: carry, clr
  Shift_Register #(.length(29)) shift_register_1 (
    .shift(controller_circuit_1_shr), .in(M29_57[28]), .clk(clock_1_out), .out(shift_register_1_out),
    .load(controller_circuit_1_load_a), .clr(controller_circuit_1_cl__a__q_1), .d0(alu_1_out_4[28]),
    .q0(M29_57[28]), .d1(alu_1_out_4[27]), .q1(M29_57[27]), .d2(alu_1_out_4[26]), .q2(M29_57[26]),
    .d3(alu_1_out_4[25]), .q3(M29_57[25]), .d4(alu_1_out_4[24]), .q4(M29_57[24]), .d5(alu_1_out_4[23]),
    .q5(M29_57[23]), .d6(alu_1_out_4[22]), .q6(M29_57[22]), .d7(alu_1_out_4[21]), .q7(M29_57[21]),
    .d8(alu_1_out_4[20]), .q8(M29_57[20]), .d9(alu_1_out_4[19]), .q9(M29_57[19]), .d10(alu_1_out_4[18]),
    .q10(M29_57[18]), .d11(alu_1_out_4[17]), .q11(M29_57[17]), .d12(alu_1_out_4[16]), .q12(M29_57[16]),
    .d13(alu_1_out_4[15]), .q13(M29_57[15]), .d14(alu_1_out_4[14]), .q14(M29_57[14]), .d15(alu_1_out_4[13]),
    .q15(M29_57[13]), .d16(alu_1_out_4[12]), .q16(M29_57[12]), .d17(alu_1_out_4[11]), .q17(M29_57[11]),
    .d18(alu_1_out_4[10]), .q18(M29_57[10]), .d19(alu_1_out_4[9]), .q19(M29_57[9]), .d20(alu_1_out_4[8]),
    .q20(M29_57[8]), .d21(alu_1_out_4[7]), .q21(M29_57[7]), .d22(alu_1_out_4[6]), .q22(M29_57[6]),
    .d23(alu_1_out_4[5]), .q23(M29_57[5]), .d24(alu_1_out_4[4]), .q24(M29_57[4]), .d25(alu_1_out_4[3]),
    .q25(M29_57[3]), .d26(alu_1_out_4[2]), .q26(M29_57[2]), .d27(alu_1_out_4[1]), .q27(M29_57[1]),
    .d28(alu_1_out_4[0]), .q28(M29_57[0]));
  _29BIT_2_S_COMPLEMENT u_29bit_2_s_complement_1 (.Inp(in_1), .out(n29bit_2_s_complement_1_out));
  _29BIT_2_S_COMPLEMENT u_29bit_2_s_complement_2 (.Inp(in_2), .out(n29bit_2_s_complement_2_out));
  Shift_Register #(.length(29)) shift_register_2 (
    .shift(1'b0), .clk(clock_1_out), .load(controller_circuit_1_load__m__q__cnt),
    .d0(n29bit_2_s_complement_1_out[28]), .q0(shift_register_2_q28[28]),
    .d1(n29bit_2_s_complement_1_out[27]), .q1(shift_register_2_q28[27]),
    .d2(n29bit_2_s_complement_1_out[26]), .q2(shift_register_2_q28[26]),
    .d3(n29bit_2_s_complement_1_out[25]), .q3(shift_register_2_q28[25]),
    .d4(n29bit_2_s_complement_1_out[24]), .q4(shift_register_2_q28[24]),
    .d5(n29bit_2_s_complement_1_out[23]), .q5(shift_register_2_q28[23]),
    .d6(n29bit_2_s_complement_1_out[22]), .q6(shift_register_2_q28[22]),
    .d7(n29bit_2_s_complement_1_out[21]), .q7(shift_register_2_q28[21]),
    .d8(n29bit_2_s_complement_1_out[20]), .q8(shift_register_2_q28[20]),
    .d9(n29bit_2_s_complement_1_out[19]), .q9(shift_register_2_q28[19]),
    .d10(n29bit_2_s_complement_1_out[18]), .q10(shift_register_2_q28[18]),
    .d11(n29bit_2_s_complement_1_out[17]), .q11(shift_register_2_q28[17]),
    .d12(n29bit_2_s_complement_1_out[16]), .q12(shift_register_2_q28[16]),
    .d13(n29bit_2_s_complement_1_out[15]), .q13(shift_register_2_q28[15]),
    .d14(n29bit_2_s_complement_1_out[14]), .q14(shift_register_2_q28[14]),
    .d15(n29bit_2_s_complement_1_out[13]), .q15(shift_register_2_q28[13]),
    .d16(n29bit_2_s_complement_1_out[12]), .q16(shift_register_2_q28[12]),
    .d17(n29bit_2_s_complement_1_out[11]), .q17(shift_register_2_q28[11]),
    .d18(n29bit_2_s_complement_1_out[10]), .q18(shift_register_2_q28[10]),
    .d19(n29bit_2_s_complement_1_out[9]), .q19(shift_register_2_q28[9]),
    .d20(n29bit_2_s_complement_1_out[8]), .q20(shift_register_2_q28[8]),
    .d21(n29bit_2_s_complement_1_out[7]), .q21(shift_register_2_q28[7]),
    .d22(n29bit_2_s_complement_1_out[6]), .q22(shift_register_2_q28[6]),
    .d23(n29bit_2_s_complement_1_out[5]), .q23(shift_register_2_q28[5]),
    .d24(n29bit_2_s_complement_1_out[4]), .q24(shift_register_2_q28[4]),
    .d25(n29bit_2_s_complement_1_out[3]), .q25(shift_register_2_q28[3]),
    .d26(n29bit_2_s_complement_1_out[2]), .q26(shift_register_2_q28[2]),
    .d27(n29bit_2_s_complement_1_out[1]), .q27(shift_register_2_q28[1]),
    .d28(n29bit_2_s_complement_1_out[0]), .q28(shift_register_2_q28[0]));  // open: in, out, clr
  ALU alu_1 (
    .Control(controller_circuit_1_c0), .in_2(M29_57), .in_3(shift_register_2_q28), .out_4(alu_1_out_4));  // open: Flags
  Shift_Register #(.length(29)) shift_register_3 (
    .shift(controller_circuit_1_shr), .in(shift_register_1_out), .clk(clock_1_out),
    .out(shift_register_3_out), .load(controller_circuit_1_load__m__q__cnt),
    .d0(n29bit_2_s_complement_2_out[28]), .q0(M0_28[28]), .d1(n29bit_2_s_complement_2_out[27]),
    .q1(M0_28[27]), .d2(n29bit_2_s_complement_2_out[26]), .q2(M0_28[26]),
    .d3(n29bit_2_s_complement_2_out[25]), .q3(M0_28[25]), .d4(n29bit_2_s_complement_2_out[24]),
    .q4(M0_28[24]), .d5(n29bit_2_s_complement_2_out[23]), .q5(M0_28[23]),
    .d6(n29bit_2_s_complement_2_out[22]), .q6(M0_28[22]), .d7(n29bit_2_s_complement_2_out[21]),
    .q7(M0_28[21]), .d8(n29bit_2_s_complement_2_out[20]), .q8(M0_28[20]),
    .d9(n29bit_2_s_complement_2_out[19]), .q9(M0_28[19]), .d10(n29bit_2_s_complement_2_out[18]),
    .q10(M0_28[18]), .d11(n29bit_2_s_complement_2_out[17]), .q11(M0_28[17]),
    .d12(n29bit_2_s_complement_2_out[16]), .q12(M0_28[16]), .d13(n29bit_2_s_complement_2_out[15]),
    .q13(M0_28[15]), .d14(n29bit_2_s_complement_2_out[14]), .q14(M0_28[14]),
    .d15(n29bit_2_s_complement_2_out[13]), .q15(M0_28[13]), .d16(n29bit_2_s_complement_2_out[12]),
    .q16(M0_28[12]), .d17(n29bit_2_s_complement_2_out[11]), .q17(M0_28[11]),
    .d18(n29bit_2_s_complement_2_out[10]), .q18(M0_28[10]), .d19(n29bit_2_s_complement_2_out[9]),
    .q19(M0_28[9]), .d20(n29bit_2_s_complement_2_out[8]), .q20(M0_28[8]),
    .d21(n29bit_2_s_complement_2_out[7]), .q21(M0_28[7]), .d22(n29bit_2_s_complement_2_out[6]),
    .q22(M0_28[6]), .d23(n29bit_2_s_complement_2_out[5]), .q23(M0_28[5]),
    .d24(n29bit_2_s_complement_2_out[4]), .q24(M0_28[4]), .d25(n29bit_2_s_complement_2_out[3]),
    .q25(M0_28[3]), .d26(n29bit_2_s_complement_2_out[2]), .q26(M0_28[2]),
    .d27(n29bit_2_s_complement_2_out[1]), .q27(M0_28[1]), .d28(n29bit_2_s_complement_2_out[0]), .q28(M0_28[0]));  // open: clr
  Shift_Register #(.length(1)) shift_register_4 (
    .shift(controller_circuit_1_shr), .in(shift_register_3_out), .clk(clock_1_out),
    .clr(controller_circuit_1_cl__a__q_1), .q0(shift_register_4_q0));  // open: out, load, d0

  // Notes on the sheet:
  //   Output
  //   A
  //   B
  //   Input
endmodule
