// Logisim project 29 Bit ALU Parallel.circ as structural Verilog: 12 circuits, main circuit main
module main (
  input  [1:0] Control,
  input  [28:0] in_2,
  input  [28:0] in_3,
  output [28:0] out_4,
  output [3:0] Flags
);

  wire zero_check_1_output;
  wire [28:0] n29bit_adder_1_out_4, n29bit_and_1_out_3, n29bit_or_1_out_3;

  _29bit_AND u_29bit_and_1 (.in_1(in_2), .in_2(in_3), .out_3(n29bit_and_1_out_3));
  _29bit_OR u_29bit_or_1 (.in_1(in_3), .in_2(in_2), .out_3(n29bit_or_1_out_3));
  _29bit_Adder u_29bit_adder_1 (
    .in_1(Control[0]), .in_2(in_2), .in_3(in_3), .out_4(n29bit_adder_1_out_4), .out_5(Flags[1]),
    .Overflow(Flags[0]));
  Multiplexer #(.select(2), .width(29), .enable("false")) multiplexer_1 (
    .in0(n29bit_adder_1_out_4), .in1(n29bit_adder_1_out_4), .in2(n29bit_and_1_out_3),
    .in3(n29bit_or_1_out_3), .out(out_4), .sel(Control));
  Negative_Check negative_check_1 (.in_1(out_4), .Output(Flags[3]));
  Zero_Check zero_check_1 (.in_1(out_4), .Output(zero_check_1_output));
  not not_1 (Flags[2], zero_check_1_output);

  // Other names for the same wires on the sheet: Overflow = Flags[0]; Carry = Flags[1]; Zero = Flags[2];
  //   Negative = Flags[3]

  // Notes on the sheet:
  //   0 0 - Adder
  //   1 0 - AND
  //   1 1 - OR
  //   0 1 - Subtractor
  //   Input
  //   A
  //   B
  //   Output
  //   Negative- Zero-Carry-Overflow
endmodule

// AND
module _29bit_AND (
  input  [28:0] in_1,
  input  [28:0] in_2,
  output [28:0] out_3
);

  assign out_3 = in_1 & in_2;  // AND_Gate and_1, 29 bits wide

  // Notes on the sheet:
  //   A
  //   B
  //   A AND B
endmodule

// OR
module _29bit_OR (
  input  [28:0] in_1,
  input  [28:0] in_2,
  output [28:0] out_3
);

  assign out_3 = in_1 | in_2;  // OR_Gate or_1, 29 bits wide

  // Notes on the sheet:
  //   A
  //   B
  //   A OR B
endmodule

// Adder
module _29bit_Adder (
  input  in_1,
  input  [28:0] in_2,
  input  [28:0] in_3,
  output [28:0] out_4,
  output out_5,
  output Overflow
);

  wire _1, _2, _3, _4, _5, _6, _7, _8, _9, _10, _11, _12, _13, _14, _15, _16, _17, _18, _19, _20, _21, _22,
       _23, _24, _25, _26, _27, _28, and_1_out, and_2_out, not_1_out, not_2_out, not_3_out;
  wire [28:0] bit_extender_1_out, xor_1_out;

  assign bit_extender_1_out = {{28{in_1}}, in_1};  // Bit_Extender bit_extender_1
  assign xor_1_out = bit_extender_1_out ^ in_3;  // XOR_Gate xor_1, 29 bits wide
  _29bit_CLG u_29bit_clg_1 (
    .Cin(in_1), .in_2(in_2), .in_3(in_3),
    .out_4({out_5, _28, _27, _26, _25, _24, _23, _22, _21, _20, _19, _18, _17, _16, _15, _14, _13, _12, _11, _10, _9, _8, _7, _6, _5, _4, _3, _2, _1}));
  _1bit_Adder u_1bit_adder_1 (.Cin(in_1), .A(in_2[0]), .B(xor_1_out[0]), .Sum(out_4[0]));  // open: Cout
  _1bit_Adder u_1bit_adder_2 (.Cin(_1), .A(in_2[1]), .B(xor_1_out[1]), .Sum(out_4[1]));  // open: Cout
  _1bit_Adder u_1bit_adder_3 (.Cin(_2), .A(in_2[2]), .B(xor_1_out[2]), .Sum(out_4[2]));  // open: Cout
  _1bit_Adder u_1bit_adder_4 (.Cin(_3), .A(in_2[3]), .B(xor_1_out[3]), .Sum(out_4[3]));  // open: Cout
  _1bit_Adder u_1bit_adder_5 (.Cin(_4), .A(in_2[4]), .B(xor_1_out[4]), .Sum(out_4[4]));  // open: Cout
  _1bit_Adder u_1bit_adder_6 (.Cin(_5), .A(in_2[5]), .B(xor_1_out[5]), .Sum(out_4[5]));  // open: Cout
  _1bit_Adder u_1bit_adder_7 (.Cin(_6), .A(in_2[6]), .B(xor_1_out[6]), .Sum(out_4[6]));  // open: Cout
  _1bit_Adder u_1bit_adder_8 (.Cin(_7), .A(in_2[7]), .B(xor_1_out[7]), .Sum(out_4[7]));  // open: Cout
  _1bit_Adder u_1bit_adder_9 (.Cin(_8), .A(in_2[8]), .B(xor_1_out[8]), .Sum(out_4[8]));  // open: Cout
  _1bit_Adder u_1bit_adder_10 (.Cin(_9), .A(in_2[9]), .B(xor_1_out[9]), .Sum(out_4[9]));  // open: Cout
  _1bit_Adder u_1bit_adder_11 (.Cin(_10), .A(in_2[10]), .B(xor_1_out[10]), .Sum(out_4[10]));  // open: Cout
  _1bit_Adder u_1bit_adder_12 (.Cin(_11), .A(in_2[11]), .B(xor_1_out[11]), .Sum(out_4[11]));  // open: Cout
  _1bit_Adder u_1bit_adder_13 (.Cin(_12), .A(in_2[12]), .B(xor_1_out[12]), .Sum(out_4[12]));  // open: Cout
  _1bit_Adder u_1bit_adder_14 (.Cin(_13), .A(in_2[13]), .B(xor_1_out[13]), .Sum(out_4[13]));  // open: Cout
  _1bit_Adder u_1bit_adder_15 (.Cin(_14), .A(in_2[14]), .B(xor_1_out[14]), .Sum(out_4[14]));  // open: Cout
  _1bit_Adder u_1bit_adder_16 (.Cin(_15), .A(in_2[15]), .B(xor_1_out[15]), .Sum(out_4[15]));  // open: Cout
  _1bit_Adder u_1bit_adder_17 (.Cin(_16), .A(in_2[16]), .B(xor_1_out[16]), .Sum(out_4[16]));  // open: Cout
  _1bit_Adder u_1bit_adder_18 (.Cin(_17), .A(in_2[17]), .B(xor_1_out[17]), .Sum(out_4[17]));  // open: Cout
  _1bit_Adder u_1bit_adder_19 (.Cin(_18), .A(in_2[18]), .B(xor_1_out[18]), .Sum(out_4[18]));  // open: Cout
  _1bit_Adder u_1bit_adder_20 (.Cin(_19), .A(in_2[19]), .B(xor_1_out[19]), .Sum(out_4[19]));  // open: Cout
  _1bit_Adder u_1bit_adder_21 (.Cin(_20), .A(in_2[20]), .B(xor_1_out[20]), .Sum(out_4[20]));  // open: Cout
  _1bit_Adder u_1bit_adder_22 (.Cin(_21), .A(in_2[21]), .B(xor_1_out[21]), .Sum(out_4[21]));  // open: Cout
  _1bit_Adder u_1bit_adder_23 (.Cin(_22), .A(in_2[22]), .B(xor_1_out[22]), .Sum(out_4[22]));  // open: Cout
  _1bit_Adder u_1bit_adder_24 (.Cin(_23), .A(in_2[23]), .B(xor_1_out[23]), .Sum(out_4[23]));  // open: Cout
  _1bit_Adder u_1bit_adder_25 (.Cin(_24), .A(in_2[24]), .B(xor_1_out[24]), .Sum(out_4[24]));  // open: Cout
  _1bit_Adder u_1bit_adder_26 (.Cin(_25), .A(in_2[25]), .B(xor_1_out[25]), .Sum(out_4[25]));  // open: Cout
  _1bit_Adder u_1bit_adder_27 (.Cin(_26), .A(in_2[26]), .B(xor_1_out[26]), .Sum(out_4[26]));  // open: Cout
  _1bit_Adder u_1bit_adder_28 (.Cin(_27), .A(in_2[27]), .B(xor_1_out[27]), .Sum(out_4[27]));  // open: Cout
  _1bit_Adder u_1bit_adder_29 (.Cin(_28), .A(in_2[28]), .B(xor_1_out[28]), .Sum(out_4[28]));  // open: Cout
  not not_1 (not_1_out, out_4[28]);
  and and_1 (and_1_out, not_1_out, in_2[28], xor_1_out[28]);
  and and_2 (and_2_out, out_4[28], not_2_out, not_3_out);
  not not_2 (not_2_out, in_2[28]);
  not not_3 (not_3_out, xor_1_out[28]);
  or or_1 (Overflow, and_1_out, and_2_out);

  // Other names for the same wires on the sheet: _29 = out_5

  // Notes on the sheet:
  //   Control ->
  //   A
  //   B
  //   Adder/Subtractor
  //   29 bit Carry Lookahead Generator
  //   SUM
  //   Carry Out
endmodule

// Adder
module _1bit_Adder (
  input  Cin,
  input  A,
  input  B,
  output Sum,
  output Cout
);

  wire and_1_out, and_2_out, xor_1_out;

  xor xor_1 (xor_1_out, A, B);
  and and_1 (and_1_out, B, A);
  xor xor_2 (Sum, Cin, xor_1_out);
  and and_2 (and_2_out, Cin, xor_1_out);
  or or_1 (Cout, and_2_out, and_1_out);
endmodule

// Zero
module Zero_Check (
  input  [28:0] in_1,
  output Output
);

  or or_1 (Output, in_1[0], in_1[1], in_1[2], in_1[3], in_1[4], in_1[5], in_1[6], in_1[7], in_1[8], in_1[9], in_1[10], in_1[11], in_1[12], in_1[13], in_1[14], in_1[15], in_1[16], in_1[17], in_1[18], in_1[19], in_1[20], in_1[21], in_1[22], in_1[23], in_1[24], in_1[25], in_1[26], in_1[27], in_1[28]);

  // Notes on the sheet:
  //   Input
endmodule

// Neg
module Negative_Check (
  input  [28:0] in_1,
  output Output
);


  assign Output = in_1[28];

  // Notes on the sheet:
  //   Input
endmodule

module _29bit_CLG (
  input  Cin,
  input  [28:0] in_2,
  input  [28:0] in_3,
  output [28:0] out_4
);

  _4bit_CLG u_4bit_clg_1 (
    .Cin(Cin), .in_2(in_2[3:0]), .in_3(in_3[3:0]), .C1(out_4[0]), .C2(out_4[1]), .C3(out_4[2]), .C4(out_4[3]));
  _4bit_CLG u_4bit_clg_2 (
    .Cin(out_4[3]), .in_2(in_2[7:4]), .in_3(in_3[7:4]), .C1(out_4[4]), .C2(out_4[5]), .C3(out_4[6]),
    .C4(out_4[7]));
  _4bit_CLG u_4bit_clg_3 (
    .Cin(out_4[7]), .in_2(in_2[11:8]), .in_3(in_3[11:8]), .C1(out_4[8]), .C2(out_4[9]), .C3(out_4[10]),
    .C4(out_4[11]));
  _4bit_CLG u_4bit_clg_4 (
    .Cin(out_4[11]), .in_2(in_2[15:12]), .in_3(in_3[15:12]), .C1(out_4[12]), .C2(out_4[13]), .C3(out_4[14]),
    .C4(out_4[15]));
  _4bit_CLG u_4bit_clg_5 (
    .Cin(out_4[15]), .in_2(in_2[19:16]), .in_3(in_3[19:16]), .C1(out_4[16]), .C2(out_4[17]), .C3(out_4[18]),
    .C4(out_4[19]));
  _4bit_CLG u_4bit_clg_6 (
    .Cin(out_4[19]), .in_2(in_2[23:20]), .in_3(in_3[23:20]), .C1(out_4[20]), .C2(out_4[21]), .C3(out_4[22]),
    .C4(out_4[23]));
  _4bit_CLG u_4bit_clg_7 (
    .Cin(out_4[23]), .in_2(in_2[27:24]), .in_3(in_3[27:24]), .C1(out_4[24]), .C2(out_4[25]), .C3(out_4[26]),
    .C4(out_4[27]));
  _1bit_carry u_1bit_carry_1 (.Cin(out_4[27]), .A(in_2[28]), .B(in_3[28]), .Cout(out_4[28]));

  // Notes on the sheet:
  //   A
  //   B
  //   Cout
endmodule

module _4bit_CLG (
  input  Cin,
  input  [3:0] in_2,
  input  [3:0] in_3,
  output C1,
  output C2,
  output C3,
  output C4
);

  wire and_1_out, and_2_out, and_3_out, and_4_out, and_5_out, and_6_out, and_7_out, and_8_out, and_9_out,
       and_10_out, and_11_out, and_12_out, and_13_out, and_14_out, xor_1_out, xor_2_out, xor_3_out,
       xor_4_out, xor_5_out, xor_6_out, xor_7_out, xor_8_out;

  xor xor_1 (xor_1_out, in_3[0], Cin);
  xor xor_2 (xor_2_out, in_3[1], Cin);
  xor xor_3 (xor_3_out, in_3[2], Cin);
  xor xor_4 (xor_4_out, in_3[3], Cin);
  xor xor_5 (xor_5_out, in_2[0], xor_1_out);
  xor xor_6 (xor_6_out, in_2[1], xor_2_out);
  xor xor_7 (xor_7_out, in_2[2], xor_3_out);
  xor xor_8 (xor_8_out, in_2[3], xor_4_out);
  and and_1 (and_1_out, in_2[0], xor_1_out);
  and and_2 (and_2_out, in_2[1], xor_2_out);
  and and_3 (and_3_out, in_2[2], xor_3_out);
  and and_4 (and_4_out, in_2[3], xor_4_out);
  and and_5 (and_5_out, Cin, xor_5_out);
  and and_6 (and_6_out, Cin, xor_5_out, xor_6_out);
  and and_7 (and_7_out, xor_6_out, and_1_out);
  and and_8 (and_8_out, xor_7_out, xor_6_out, xor_5_out, Cin);
  and and_9 (and_9_out, and_1_out, xor_6_out, xor_7_out);
  and and_10 (and_10_out, xor_7_out, and_2_out);
  and and_11 (and_11_out, xor_8_out, and_3_out);
  and and_12 (and_12_out, xor_8_out, xor_7_out, and_2_out);
  and and_13 (and_13_out, xor_8_out, xor_7_out, xor_6_out, and_1_out);
  and and_14 (and_14_out, xor_8_out, xor_7_out, xor_6_out, xor_5_out, Cin);
  or or_1 (C1, and_5_out, and_1_out);
  or or_2 (C2, and_6_out, and_7_out, and_2_out);
  or or_3 (C3, and_8_out, and_9_out, and_10_out, and_3_out);
  or or_4 (C4, and_14_out, and_13_out, and_12_out, and_11_out, and_4_out);

  // Notes on the sheet:
  //   A
  //   B
endmodule

// 1bit CLG
module _1bit_carry (
  input  Cin,
  input  A,
  input  B,
  output Cout
);

  wire and_1_out, and_2_out, xor_1_out, xor_2_out;

  xor xor_1 (xor_1_out, Cin, B);
  and and_1 (and_1_out, A, xor_1_out);
  xor xor_2 (xor_2_out, A, xor_1_out);
  and and_2 (and_2_out, xor_2_out, Cin);
  or or_1 (Cout, and_1_out, and_2_out);
endmodule

module _4_bit_Parallel_Adder (
  input  [3:0] in_1,
  input  [3:0] in_2,
  input  [3:0] in_3,
  output [3:0] out_4
);

  _1bit_Adder u_1bit_adder_1 (.Cin(in_1[0]), .A(in_2[0]), .B(in_3[0]), .Sum(out_4[0]));  // open: Cout
  _1bit_Adder u_1bit_adder_2 (.Cin(in_1[1]), .A(in_2[1]), .B(in_3[1]), .Sum(out_4[1]));  // open: Cout
  _1bit_Adder u_1bit_adder_3 (.Cin(in_1[2]), .A(in_2[2]), .B(in_3[2]), .Sum(out_4[2]));  // open: Cout
  _1bit_Adder u_1bit_adder_4 (.Cin(in_1[3]), .A(in_2[3]), .B(in_3[3]), .Sum(out_4[3]));  // open: Cout
endmodule

module _29_bit_Parallel_Adder (
  input  in_1,
  input  [28:0] in_2,
  input  [28:0] in_3,
  output [28:0] out_4,
  output out_5,
  output out_6
);

  wire and_1_out, and_2_out, not_1_out, not_2_out, not_3_out;
  wire [27:0] n29bit_clg_1_out_4;
  wire [28:0] bit_extender_1_out, xor_1_out;

  assign bit_extender_1_out = {{28{in_1}}, in_1};  // Bit_Extender bit_extender_1
  _29bit_CLG u_29bit_clg_1 (.Cin(in_1), .in_2(in_2), .in_3(in_3), .out_4({out_5, n29bit_clg_1_out_4}));
  assign xor_1_out = in_3 ^ bit_extender_1_out;  // XOR_Gate xor_1, 29 bits wide
  _4_bit_Parallel_Adder u_4_bit_parallel_adder_1 (
    .in_1({n29bit_clg_1_out_4[2:0], in_1}), .in_2(in_2[3:0]), .in_3(xor_1_out[3:0]), .out_4(out_4[3:0]));
  _4_bit_Parallel_Adder u_4_bit_parallel_adder_2 (
    .in_1(n29bit_clg_1_out_4[6:3]), .in_2(in_2[7:4]), .in_3(xor_1_out[7:4]), .out_4(out_4[7:4]));
  _4_bit_Parallel_Adder u_4_bit_parallel_adder_3 (
    .in_1(n29bit_clg_1_out_4[10:7]), .in_2(in_2[11:8]), .in_3(xor_1_out[11:8]), .out_4(out_4[11:8]));
  _4_bit_Parallel_Adder u_4_bit_parallel_adder_4 (
    .in_1(n29bit_clg_1_out_4[14:11]), .in_2(in_2[15:12]), .in_3(xor_1_out[15:12]), .out_4(out_4[15:12]));
  _4_bit_Parallel_Adder u_4_bit_parallel_adder_5 (
    .in_1(n29bit_clg_1_out_4[18:15]), .in_2(in_2[19:16]), .in_3(xor_1_out[19:16]), .out_4(out_4[19:16]));
  _4_bit_Parallel_Adder u_4_bit_parallel_adder_6 (
    .in_1(n29bit_clg_1_out_4[22:19]), .in_2(in_2[23:20]), .in_3(xor_1_out[23:20]), .out_4(out_4[23:20]));
  _4_bit_Parallel_Adder u_4_bit_parallel_adder_7 (
    .in_1(n29bit_clg_1_out_4[26:23]), .in_2(in_2[27:24]), .in_3(xor_1_out[27:24]), .out_4(out_4[27:24]));
  _1bit_Adder u_1bit_adder_1 (
    .Cin(n29bit_clg_1_out_4[27]), .A(in_2[28]), .B(xor_1_out[28]), .Sum(out_4[28]));  // open: Cout
  not not_1 (not_1_out, in_2[28]);
  not not_2 (not_2_out, xor_1_out[28]);
  not not_3 (not_3_out, out_4[28]);
  and and_1 (and_1_out, not_1_out, not_2_out, out_4[28]);
  and and_2 (and_2_out, not_3_out, in_2[28], xor_1_out[28]);
  or or_1 (out_6, and_1_out, and_2_out);

  // Notes on the sheet:
  //   A
  //   B
endmodule
