// Logisim project CPU.circ as structural Verilog: 17 circuits, main circuit 4BIT-PLR
module _4BIT_PLR (
  input  Load,
  input  [3:0] Input,
  input  Clock,
  input  Reset,
  output [3:0] Output
);

  wire and_1_out, and_2_out, and_3_out, and_4_out, and_5_out, and_6_out, and_7_out, and_8_out, not_1_out,
       not_2_out, not_3_out, not_4_out;

  not not_1 (not_1_out, Input[0]);
  not not_2 (not_2_out, Input[1]);
  not not_3 (not_3_out, Input[2]);
  not not_4 (not_4_out, Input[3]);
  and and_1 (and_1_out, Input[0], Load);
  and and_2 (and_2_out, not_1_out, Load);
  and and_3 (and_3_out, Input[1], Load);
  and and_4 (and_4_out, not_2_out, Load);
  and and_5 (and_5_out, Input[2], Load);
  and and_6 (and_6_out, not_3_out, Load);
  and and_7 (and_7_out, Input[3], Load);
  and and_8 (and_8_out, not_4_out, Load);
  J_K_Flip_Flop j_k_ff_1 (
    .J(and_1_out), .clk(Clock), .K(and_2_out), .Q(Output[0]), .reset(Reset));  // open: Qn, preset, en
  J_K_Flip_Flop j_k_ff_2 (
    .J(and_3_out), .clk(Clock), .K(and_4_out), .Q(Output[1]), .reset(Reset));  // open: Qn, preset, en
  J_K_Flip_Flop j_k_ff_3 (
    .J(and_5_out), .clk(Clock), .K(and_6_out), .Q(Output[2]), .reset(Reset));  // open: Qn, preset, en
  J_K_Flip_Flop j_k_ff_4 (
    .J(and_7_out), .clk(Clock), .K(and_8_out), .Q(Output[3]), .reset(Reset));  // open: Qn, preset, en

  // Notes on the sheet:
  //   MD. SABBIR HOSSAIN
endmodule

module _4BIT_CPLR (
  input  Cin,
  input  Count,
  input  Load,
  input  [3:0] Input,
  input  Clock,
  input  Reset,
  output [3:0] Output,
  output Cout
);

  wire and_1_out, and_2_out, and_3_out, and_4_out, and_5_out, and_6_out, and_7_out, and_8_out, and_9_out,
       and_10_out, and_11_out, and_12_out, and_13_out, not_1_out, not_2_out, not_3_out, not_4_out, not_5_out,
       or_1_out, or_2_out, or_3_out, or_4_out, or_5_out, or_6_out, or_7_out, or_8_out;

  not not_1 (not_1_out, Load);
  and and_1 (and_1_out, Count, not_1_out);
  not not_2 (not_2_out, Input[0]);
  not not_3 (not_3_out, Input[1]);
  not not_4 (not_4_out, Input[2]);
  not not_5 (not_5_out, Input[3]);
  and and_2 (and_2_out, Load, Input[0]);
  and and_3 (and_3_out, Load, not_2_out);
  and and_4 (and_4_out, Load, Input[1]);
  and and_5 (and_5_out, Load, not_3_out);
  and and_6 (and_6_out, Load, Input[2]);
  and and_7 (and_7_out, Load, not_4_out);
  and and_8 (and_8_out, Load, Input[3]);
  and and_9 (and_9_out, Load, not_5_out);
  and and_10 (and_10_out, and_1_out, Cin);
  and and_11 (and_11_out, and_1_out, Cin, Output[0]);
  and and_12 (and_12_out, Cin, Output[1], Output[2], and_1_out, Output[0]);
  or or_1 (or_1_out, and_2_out, and_10_out);
  or or_2 (or_2_out, and_10_out, and_3_out);
  or or_3 (or_3_out, and_4_out, and_11_out);
  or or_4 (or_4_out, and_11_out, and_5_out);
  and and_13 (and_13_out, Output[0], Cin, Output[1], and_1_out);
  or or_5 (or_5_out, and_6_out, and_13_out);
  or or_6 (or_6_out, and_13_out, and_7_out);
  or or_7 (or_7_out, and_8_out, and_12_out);
  or or_8 (or_8_out, and_12_out, and_9_out);
  J_K_Flip_Flop j_k_ff_1 (
    .J(or_1_out), .clk(Clock), .K(or_2_out), .Q(Output[0]), .reset(Reset));  // open: Qn, preset, en
  J_K_Flip_Flop j_k_ff_2 (
    .J(or_3_out), .clk(Clock), .K(or_4_out), .Q(Output[1]), .reset(Reset));  // open: Qn, preset, en
  J_K_Flip_Flop j_k_ff_3 (
    .J(or_7_out), .clk(Clock), .K(or_8_out), .Q(Output[3]), .reset(Reset));  // open: Qn, preset, en
  J_K_Flip_Flop j_k_ff_4 (
    .J(or_5_out), .clk(Clock), .K(or_6_out), .Q(Output[2]), .reset(Reset));  // open: Qn, preset, en
  and and_14 (Cout, Output[0], Cin, Output[1], Output[2], Output[3], and_1_out);

  // Notes on the sheet:
  //   MD. SABBIR HOSSAIN
endmodule

module _2BIT_PLR (
  input  Load,
  input  [1:0] Input,
  input  Clock,
  input  Reset,
  output [1:0] Output
);

  wire and_1_out, and_2_out, and_3_out, and_4_out, not_1_out, not_2_out;

  not not_1 (not_1_out, Input[0]);
  not not_2 (not_2_out, Input[1]);
  and and_1 (and_1_out, Input[0], Load);
  and and_2 (and_2_out, not_1_out, Load);
  and and_3 (and_3_out, Input[1], Load);
  and and_4 (and_4_out, not_2_out, Load);
  J_K_Flip_Flop j_k_ff_1 (
    .J(and_1_out), .clk(Clock), .K(and_2_out), .Q(Output[0]), .reset(Reset));  // open: Qn, preset, en
  J_K_Flip_Flop j_k_ff_2 (
    .J(and_3_out), .clk(Clock), .K(and_4_out), .Q(Output[1]), .reset(Reset));  // open: Qn, preset, en

  // Notes on the sheet:
  //   MD. SABBIR HOSSAIN
endmodule

module _2BIT_CPLR (
  input  Cin,
  input  Count,
  input  Load,
  input  [1:0] Input,
  input  Clock,
  input  Reset,
  output [1:0] Output
);

  wire and_1_out, and_2_out, and_3_out, and_4_out, and_5_out, and_6_out, and_7_out, not_1_out, not_2_out,
       not_3_out, or_1_out, or_2_out, or_3_out, or_4_out;

  not not_1 (not_1_out, Load);
  not not_2 (not_2_out, Input[0]);
  not not_3 (not_3_out, Input[1]);
  and and_1 (and_1_out, Count, not_1_out);
  and and_2 (and_2_out, Load, Input[0]);
  and and_3 (and_3_out, Load, not_2_out);
  and and_4 (and_4_out, Load, Input[1]);
  and and_5 (and_5_out, Load, not_3_out);
  and and_6 (and_6_out, and_1_out, Cin);
  and and_7 (and_7_out, and_1_out, Cin, Output[0]);
  or or_1 (or_1_out, and_2_out, and_6_out);
  or or_2 (or_2_out, and_6_out, and_3_out);
  or or_3 (or_3_out, and_4_out, and_7_out);
  or or_4 (or_4_out, and_7_out, and_5_out);
  J_K_Flip_Flop j_k_ff_1 (
    .J(or_1_out), .clk(Clock), .K(or_2_out), .Q(Output[0]), .reset(Reset));  // open: Qn, preset, en
  J_K_Flip_Flop j_k_ff_2 (
    .J(or_3_out), .clk(Clock), .K(or_4_out), .Q(Output[1]), .reset(Reset));  // open: Qn, preset, en

  // Notes on the sheet:
  //   MD. SABBIR HOSSAIN
endmodule

module _1BIT_PLR (
  input  Load,
  input  Input,
  input  Clock,
  input  Reset,
  output Output
);

  wire and_1_out, and_2_out, not_1_out;

  not not_1 (not_1_out, Input);
  and and_1 (and_1_out, Input, Load);
  and and_2 (and_2_out, not_1_out, Load);
  J_K_Flip_Flop j_k_ff_1 (
    .J(and_1_out), .clk(Clock), .K(and_2_out), .Q(Output), .reset(Reset));  // open: Qn, preset, en

  // Notes on the sheet:
  //   MD. SABBIR HOSSAIN
endmodule

module _1BIT_CPLR (
  input  Cin,
  input  Count,
  input  Load,
  input  Input,
  input  Clock,
  input  Reset,
  output Output
);

  wire and_1_out, and_2_out, and_3_out, and_4_out, not_1_out, not_2_out, or_1_out, or_2_out;

  not not_1 (not_1_out, Load);
  and and_1 (and_1_out, Count, not_1_out);
  not not_2 (not_2_out, Input);
  and and_2 (and_2_out, Load, Input);
  and and_3 (and_3_out, Load, not_2_out);
  and and_4 (and_4_out, and_1_out, Cin);
  or or_1 (or_1_out, and_2_out, and_4_out);
  or or_2 (or_2_out, and_4_out, and_3_out);
  J_K_Flip_Flop j_k_ff_1 (.J(or_1_out), .clk(Clock), .K(or_2_out), .Q(Output), .reset(Reset));  // open: Qn, preset, en

  // Notes on the sheet:
  //   MD. SABBIR HOSSAIN
endmodule

module IR (
  input  Load,
  input  [3:0] Input,
  input  Clock,
  input  Reset,
  output [3:0] Output
);

  _4BIT_PLR u_4bit_plr_1 (.Load(Load), .Input(Input), .Clock(Clock), .Reset(Reset), .Output(Output));

  // Notes on the sheet:
  //   MD. SABBIR HOSSAIN
endmodule

module PC (
  input  Load,
  input  Count,
  input  [5:0] Input,
  input  Clock,
  input  Reset,
  output [5:0] Output
);

  wire n4bit_cplr_1_cout;

  _4BIT_CPLR u_4bit_cplr_1 (
    .Cin(Count), .Count(Count), .Load(Load), .Input(Input[3:0]), .Clock(Clock), .Reset(Reset),
    .Output(Output[3:0]), .Cout(n4bit_cplr_1_cout));
  _2BIT_CPLR u_2bit_cplr_1 (
    .Cin(n4bit_cplr_1_cout), .Count(Count), .Load(Load), .Input(Input[5:4]), .Clock(Clock), .Reset(Reset),
    .Output(Output[5:4]));

  // Notes on the sheet:
  //   MD. SABBIR HOSSAIN
endmodule

module MAR (
  input  Load,
  input  [5:0] Input,
  input  Clock,
  input  Reset,
  output [5:0] out_5
);

  _4BIT_PLR u_4bit_plr_1 (.Load(Load), .Input(Input[3:0]), .Clock(Clock), .Reset(Reset), .Output(out_5[3:0]));
  _2BIT_PLR u_2bit_plr_1 (.Load(Load), .Input(Input[5:4]), .Clock(Clock), .Reset(Reset), .Output(out_5[5:4]));

  // Notes on the sheet:
  //   MD. SABBIR HOSSAIN
endmodule

module _29BIT_MBR (
  input  Load,
  input  Count,
  input  [28:0] Input,
  input  Clock,
  input  Reset,
  output [28:0] Output
);

  wire n4bit_cplr_1_cout, n4bit_cplr_2_cout, n4bit_cplr_3_cout, n4bit_cplr_4_cout, n4bit_cplr_5_cout,
       n4bit_cplr_6_cout, n4bit_cplr_7_cout;

  _4BIT_CPLR u_4bit_cplr_1 (
    .Cin(Count), .Count(Count), .Load(Load), .Input(Input[3:0]), .Clock(Clock), .Reset(Reset),
    .Output(Output[3:0]), .Cout(n4bit_cplr_1_cout));
  _4BIT_CPLR u_4bit_cplr_2 (
    .Cin(n4bit_cplr_1_cout), .Count(Count), .Load(Load), .Input(Input[7:4]), .Clock(Clock), .Reset(Reset),
    .Output(Output[7:4]), .Cout(n4bit_cplr_2_cout));
  _4BIT_CPLR u_4bit_cplr_3 (
    .Cin(n4bit_cplr_2_cout), .Count(Count), .Load(Load), .Input(Input[11:8]), .Clock(Clock), .Reset(Reset),
    .Output(Output[11:8]), .Cout(n4bit_cplr_3_cout));
  _4BIT_CPLR u_4bit_cplr_4 (
    .Cin(n4bit_cplr_3_cout), .Count(Count), .Load(Load), .Input(Input[15:12]), .Clock(Clock), .Reset(Reset),
    .Output(Output[15:12]), .Cout(n4bit_cplr_4_cout));
  _4BIT_CPLR u_4bit_cplr_5 (
    .Cin(n4bit_cplr_4_cout), .Count(Count), .Load(Load), .Input(Input[19:16]), .Clock(Clock), .Reset(Reset),
    .Output(Output[19:16]), .Cout(n4bit_cplr_5_cout));
  _4BIT_CPLR u_4bit_cplr_6 (
    .Cin(n4bit_cplr_5_cout), .Count(Count), .Load(Load), .Input(Input[23:20]), .Clock(Clock), .Reset(Reset),
    .Output(Output[23:20]), .Cout(n4bit_cplr_6_cout));
  _4BIT_CPLR u_4bit_cplr_7 (
    .Cin(n4bit_cplr_6_cout), .Count(Count), .Load(Load), .Input(Input[27:24]), .Clock(Clock), .Reset(Reset),
    .Output(Output[27:24]), .Cout(n4bit_cplr_7_cout));
  _1BIT_CPLR u_1bit_cplr_1 (
    .Cin(n4bit_cplr_7_cout), .Count(Count), .Load(Load), .Input(Input[28]), .Clock(Clock), .Reset(Reset),
    .Output(Output[28]));

  // Notes on the sheet:
  //   MD. SABBIR HOSSAIN
endmodule

module _29BIT_AC (
  input  Load,
  input  [28:0] Input,
  input  Clock,
  input  Reset,
  output [28:0] Output
);

  _4BIT_PLR u_4bit_plr_1 (.Load(Load), .Input(Input[3:0]), .Clock(Clock), .Reset(Reset), .Output(Output[3:0]));
  _4BIT_PLR u_4bit_plr_2 (.Load(Load), .Input(Input[7:4]), .Clock(Clock), .Reset(Reset), .Output(Output[7:4]));
  _4BIT_PLR u_4bit_plr_3 (.Load(Load), .Input(Input[11:8]), .Clock(Clock), .Reset(Reset), .Output(Output[11:8]));
  _4BIT_PLR u_4bit_plr_4 (.Load(Load), .Input(Input[15:12]), .Clock(Clock), .Reset(Reset), .Output(Output[15:12]));
  _4BIT_PLR u_4bit_plr_5 (.Load(Load), .Input(Input[19:16]), .Clock(Clock), .Reset(Reset), .Output(Output[19:16]));
  _4BIT_PLR u_4bit_plr_6 (.Load(Load), .Input(Input[23:20]), .Clock(Clock), .Reset(Reset), .Output(Output[23:20]));
  _4BIT_PLR u_4bit_plr_7 (.Load(Load), .Input(Input[27:24]), .Clock(Clock), .Reset(Reset), .Output(Output[27:24]));
  _1BIT_PLR u_1bit_plr_1 (.Load(Load), .Input(Input[28]), .Clock(Clock), .Reset(Reset), .Output(Output[28]));

  // Notes on the sheet:
  //   MD. SABBIR HOSSAIN
endmodule

module CONTRO_UNIT (
  input  [28:0] Data_In,
  input  Reset,
  input  Clock,
  output [28:0] Data_out,
  output OUT_CLOCK,
  output Store,
  output [5:0] MAR_OUT,
  output Load
);

  wire _2sC, _3, _4, _5, ACCtoMBR, ADD, ALU_ADD, ALU_AND, ALU_plus_plus, AND, and_20_out, BSB, change_to_0,
       change_to_1, CNG_OPCODE, Fetch, HALT, INC, ISZ, JMP, LOAD_t, LS, MBR_INC, MBR_INC_2, MBR_Zero,
       MBRtoACC, MBRtoIR, MBRtoMAR, MBRtoMEM_1, MBRtoMEM_2, MBRtoMEM_3, MBRtoMEM_4, MBRtoMEM_5, MBRtoMEM_6,
       MBRtoMEM_7, MBRtoPC_1, MEMtoMBR_1, MEMtoMBR_2, not_1_out, not_2_out, not_3_out, not_5_out, or_2_out,
       or_3_out, or_4_out, or_6_out, or_7_out, or_8_out, or_9_out, or_10_out, or_11_out, or_12_out,
       or_13_out, PC_INC_2, PCtoMAR, RS, STO, t0, t1, t2, t3, tunnel;
  wire [1:0] alu_selection_1_out_3, counter_1_q, multiplexer_4_out;
  wire [3:0] bit_extender_1_out, FLAG_IN, IR_OUT;
  wire [5:0] Address, multiplexer_8_out, multiplexer_9_out;
  wire [27:0] NewMBR;
  wire [28:0] ACC_IN, ACC_OUT, left_shift_1_out_2, main_1_out_4, multiplexer_2_out, multiplexer_3_out,
       multiplexer_5_out, multiplexer_7_out, n2_s_complement_1_out_2, right_shift_1_out_2;
  wire [28:6] MBR_OUT;

  _2_S_COMPLEMENT u_2_s_complement_1 (.in_1({MBR_OUT, Address}), .out_2(n2_s_complement_1_out_2));
  Decoder #(.select(2), .enable("false")) decoder_1 (.out0(t0), .out1(t1), .out2(t2), .out3(t3), .sel(counter_1_q));
  Counter #(.width(2), .max('h3)) counter_1 (
    .Q(counter_1_q), .clk(OUT_CLOCK), .clr(Reset));  // open: load, D, count, carry
  Decoder #(.select(4), .enable("false")) decoder_2 (
    .out0(AND), .out1(ADD), .out2(STO), .out3(ISZ), .out4(BSB), .out5(JMP), .out6(LOAD_t), .out7(HALT),
    .out8(INC), .out9(tunnel), .out10(_2sC), .out11(LS), .out12(RS), .out13(_3), .out14(_4), .out15(_5),
    .sel(IR_OUT));
  not not_1 (not_1_out, Fetch);
  and and_1 (PCtoMAR, not_1_out, t0);
  not not_2 (not_2_out, Fetch);
  and and_2 (MEMtoMBR_1, not_2_out, t1);
  not not_3 (not_3_out, Fetch);
  and and_3 (MBRtoIR, not_3_out, t2);
  and and_4 (ALU_AND, Fetch, t2, AND);
  and and_5 (ALU_ADD, Fetch, t2, ADD);
  and and_6 (ACCtoMBR, Fetch, t2, STO);
  and and_7 (MBRtoACC, Fetch, t2, LOAD_t);
  and and_8 (MBR_INC_2, Fetch, t2, INC);
  and and_9 (MBRtoMEM_4, Fetch, t3, INC);
  or or_1 (Store, MBRtoMEM_6, MBRtoMEM_1, MBRtoMEM_2, MBRtoMEM_7, MBRtoMEM_3, MBRtoMEM_4, MBRtoMEM_5);
  RIGHT_SHIFT right_shift_1 (.in_1({MBR_OUT, Address}), .out_2(right_shift_1_out_2));
  LEFT_SHIFT left_shift_1 (.in_1({MBR_OUT, Address}), .out_2(left_shift_1_out_2));
  Multiplexer #(.width(29), .enable("false")) multiplexer_1 (
    .in0(Data_In), .in1(multiplexer_2_out), .out(Data_out), .sel(Store));
  Multiplexer #(.select(2), .width(29), .enable("false")) multiplexer_2 (
    .in0({MBR_OUT, Address}), .in1(right_shift_1_out_2), .in2(left_shift_1_out_2),
    .in3(n2_s_complement_1_out_2), .out(multiplexer_2_out), .sel(multiplexer_4_out));
  assign bit_extender_1_out = {{3{CNG_OPCODE}}, CNG_OPCODE};  // Bit_Extender bit_extender_1
  assign NewMBR[27:24] = bit_extender_1_out & 4'b0101;  // AND_Gate and_10, 4 bits wide
  Multiplexer #(.width(29), .enable("false")) multiplexer_3 (
    .in0(ACC_IN), .in1({MBR_OUT, Address}), .out(multiplexer_3_out), .sel(MBRtoACC));
  Multiplexer #(.width(2), .enable("false")) multiplexer_4 (
    .in0({LS, RS}), .in1({1'b1, _2sC}), .out(multiplexer_4_out), .sel(_2sC));
  or or_2 (or_2_out, ALU_ADD, ALU_plus_plus, ALU_AND, MBRtoACC);
  or or_3 (or_3_out, Address[0], Address[1], Address[2], Address[3], Address[4], Address[5], MBR_OUT[6], MBR_OUT[7], MBR_OUT[8], MBR_OUT[9], MBR_OUT[10], MBR_OUT[11], MBR_OUT[12], MBR_OUT[13], MBR_OUT[14], MBR_OUT[15], MBR_OUT[16], MBR_OUT[17], MBR_OUT[18], MBR_OUT[19], MBR_OUT[20], MBR_OUT[21], MBR_OUT[22], MBR_OUT[23], MBR_OUT[24], MBR_OUT[25], MBR_OUT[26], MBR_OUT[27], MBR_OUT[28]);
  _29BIT_AC u_29bit_ac_1 (
    .Load(or_2_out), .Input(multiplexer_3_out), .Clock(OUT_CLOCK), .Reset(Reset), .Output(ACC_OUT));
  not not_4 (MBR_Zero, or_3_out);
  and and_11 (MBRtoMEM_2, Fetch, t3, ISZ);
  and and_12 (CNG_OPCODE, Fetch, t2, BSB);
  J_K_Flip_Flop j_k_ff_1 (.J(change_to_1), .clk(OUT_CLOCK), .K(change_to_0), .Q(Fetch));  // open: Qn, preset, en, reset
  and and_13 (MBRtoPC_1, JMP, t3);
  and and_14 (MBRtoMAR, Fetch, ~tunnel, t0);  // AND_Gate
  and and_15 (MBRtoMEM_3, Fetch, t3, STO);
  and and_16 (MBR_INC, Fetch, t2, ISZ);
  and and_17 (MBRtoMEM_1, Fetch, t3, BSB);
  and and_18 (ALU_plus_plus, Fetch, t0, tunnel);
  and and_19 (MBRtoMEM_7, Fetch, t3, _2sC);
  or or_4 (or_4_out, ALU_ADD, ALU_AND);
  ALU_SELECTION alu_selection_1 (.x1(ALU_ADD), .x2(ALU_AND), .out_3(alu_selection_1_out_3));
  _29_Bit_ALU_Parallel_main main_1 (
    .Control(alu_selection_1_out_3), .in_2(ACC_OUT), .in_3(multiplexer_7_out), .out_4(main_1_out_4),
    .Flags(FLAG_IN));
  or or_5 (Load, MEMtoMBR_1, MEMtoMBR_2);
  Multiplexer #(.select(2), .width(29), .enable("false")) multiplexer_5 (
    .in0(Data_In), .in1({1'b0, NewMBR[27:24], {18{1'b0}}, NewMBR[5:0]}), .in2(ACC_OUT),
    .out(multiplexer_5_out), .sel({ACCtoMBR, CNG_OPCODE}));  // open: in3
  IR ir_1 (.Load(MBRtoIR), .Input(MBR_OUT[27:24]), .Clock(OUT_CLOCK), .Reset(Reset), .Output(IR_OUT));
  Multiplexer #(.width(29), .enable("false")) multiplexer_6 (
    .in0(ACC_OUT), .in1(main_1_out_4), .out(ACC_IN), .sel(or_6_out));
  and and_20 (and_20_out, or_4_out, t2);
  Multiplexer #(.width(29), .enable("false")) multiplexer_7 (
    .in0({MBR_OUT, Address}), .in1(29'h1), .out(multiplexer_7_out), .sel(ALU_plus_plus));
  and and_21 (change_to_0, Fetch, t3);
  or or_6 (or_6_out, and_20_out, ALU_plus_plus);
  or or_7 (or_7_out, Load, ACCtoMBR, CNG_OPCODE);
  or or_8 (or_8_out, MBR_INC, MBR_INC_2);
  or or_9 (or_9_out, AND, ADD, ISZ, LOAD_t, INC, tunnel, _2sC, LS, RS, _3, _4, _5);
  and and_22 (PC_INC_2, Fetch, t3, MBR_Zero, ISZ);
  and and_23 (OUT_CLOCK, Clock, ~HALT);  // AND_Gate
  and and_24 (MBRtoMEM_5, Fetch, t3, LS);
  and and_25 (MBRtoMEM_6, Fetch, t3, RS);
  _29BIT_MBR u_29bit_mbr_1 (
    .Load(or_7_out), .Count(or_8_out), .Input(multiplexer_5_out), .Clock(OUT_CLOCK), .Reset(Reset),
    .Output({MBR_OUT, Address}));
  // Probe on {MBR_OUT, Address}
  and and_26 (MEMtoMBR_2, Fetch, t1, or_9_out);
  Multiplexer #(.width(6), .enable("false")) multiplexer_8 (
    .in0(NewMBR[5:0]), .in1(Address), .out(multiplexer_8_out), .sel(MBRtoMAR));
  or or_10 (or_10_out, AND, ADD, STO, ISZ, BSB, LOAD_t, HALT, INC, tunnel, _2sC, LS, RS, _3, _4, _5);
  Multiplexer #(.width(6), .enable("false")) multiplexer_9 (
    .in0(MAR_OUT), .in1(Address), .out(multiplexer_9_out), .sel(MBRtoPC_1));
  or or_11 (or_11_out, MEMtoMBR_1, PC_INC_2, MBRtoMEM_1);
  not not_5 (not_5_out, Fetch);
  and and_27 (change_to_1, not_5_out, t3, or_10_out);
  or or_12 (or_12_out, PCtoMAR, MBRtoMAR);
  or or_13 (or_13_out, CNG_OPCODE, MBRtoPC_1);
  PC pc_1 (
    .Load(or_13_out), .Count(or_11_out), .Input(multiplexer_9_out), .Clock(OUT_CLOCK), .Reset(Reset),
    .Output(NewMBR[5:0]));
  MAR mar_1 (.Load(or_12_out), .Input(multiplexer_8_out), .Clock(OUT_CLOCK), .Reset(Reset), .out_5(MAR_OUT));
  // Probe on NewMBR[5:0]

  // Other names for the same wires on the sheet: MARtoPC = CNG_OPCODE; PCtoMBR = CNG_OPCODE; Clock_t = OUT_CLOCK;
  //   MBR_OUT[5:0] = Address; Opcode[3:0] = MBR_OUT[27:24]; PC_out[5:0] = NewMBR[5:0]; PC_INC_1 = MEMtoMBR_1;
  //   PC_INC_3 = MBRtoMEM_1

  // Notes on the sheet:
  //   MD. SABBIR HOSSAIN
endmodule

module ALU_SELECTION (
  input  x1,
  input  x2,
  output [1:0] out_3
);


  assign out_3 = {x2, 1'b0};

  // Notes on the sheet:
  //   MD. SABBIR HOSSAIN
endmodule

module RIGHT_SHIFT (
  input  [28:0] in_1,
  output [28:0] out_2
);


  assign out_2 = {1'b0, in_1[28:1]};

  // Notes on the sheet:
  //   MD. SABBIR HOSSAIN
endmodule

module LEFT_SHIFT (
  input  [28:0] in_1,
  output [28:0] out_2
);


  assign out_2 = {in_1[27:0], 1'b0};

  // Notes on the sheet:
  //   MD. SABBIR HOSSAIN
endmodule

module _2_S_COMPLEMENT (
  input  [28:0] in_1,
  output [28:0] out_2
);

  wire [28:0] not_1_out;

  not not_1 (not_1_out[0], in_1[0]);
  not not_2 (not_1_out[1], in_1[1]);
  not not_3 (not_1_out[2], in_1[2]);
  not not_4 (not_1_out[3], in_1[3]);
  not not_5 (not_1_out[4], in_1[4]);
  not not_6 (not_1_out[5], in_1[5]);
  not not_7 (not_1_out[6], in_1[6]);
  not not_8 (not_1_out[7], in_1[7]);
  not not_9 (not_1_out[8], in_1[8]);
  not not_10 (not_1_out[9], in_1[9]);
  not not_11 (not_1_out[10], in_1[10]);
  not not_12 (not_1_out[11], in_1[11]);
  not not_13 (not_1_out[12], in_1[12]);
  not not_14 (not_1_out[13], in_1[13]);
  not not_15 (not_1_out[14], in_1[14]);
  not not_16 (not_1_out[15], in_1[15]);
  not not_17 (not_1_out[16], in_1[16]);
  not not_18 (not_1_out[17], in_1[17]);
  not not_19 (not_1_out[18], in_1[18]);
  not not_20 (not_1_out[19], in_1[19]);
  not not_21 (not_1_out[20], in_1[20]);
  not not_22 (not_1_out[21], in_1[21]);
  not not_23 (not_1_out[22], in_1[22]);
  not not_24 (not_1_out[23], in_1[23]);
  not not_25 (not_1_out[24], in_1[24]);
  not not_26 (not_1_out[25], in_1[25]);
  not not_27 (not_1_out[26], in_1[26]);
  not not_28 (not_1_out[27], in_1[27]);
  not not_29 (not_1_out[28], in_1[28]);
  _29_Bit_ALU_Parallel_main main_1 (.Control(2'b00), .in_2(not_1_out), .in_3(29'h1), .out_4(out_2));  // open: Flags

  // Notes on the sheet:
  //   MD. SABBIR HOSSAIN
endmodule

module MY_COMPUTER (
  input  in_1
);

  wire clock_1_out, contro_unit_1_load, contro_unit_1_out_clock, contro_unit_1_store;
  wire [5:0] contro_unit_1_mar_out;
  wire [28:0] contro_unit_1_data_out, ram_1_data;

  Clock clock_1 (.out(clock_1_out));
  CONTRO_UNIT contro_unit_1 (
    .Data_In(ram_1_data), .Reset(in_1), .Clock(clock_1_out), .Data_out(contro_unit_1_data_out),
    .MAR_OUT(contro_unit_1_mar_out), .OUT_CLOCK(contro_unit_1_out_clock), .Load(contro_unit_1_load),
    .Store(contro_unit_1_store));
  RAM #(.addrWidth(6), .dataWidth(29), .bus("separate")) ram_1 (
    .addr(contro_unit_1_mar_out), .din(contro_unit_1_data_out), .data(ram_1_data), .str(contro_unit_1_store),
    .clk(contro_unit_1_out_clock), .ld(contro_unit_1_load));  // open: sel, clr

  // Notes on the sheet:
  //   MD. SABBIR HOSSAIN
  //   0 - AND
  //   1 - ADD
  //   2 - STORE
  //   3 - ISZ
  //   4 - BSB
  //   5 - JMP
  //   6 - LOAD
  //   7 - HLT
  //   8 - INC
  //   9 - MINC
  //   a - 2SC
  //   b - LS
  //   c - RS
  //   Performing bitwise and operation
  //   Checks if value of mbr is zero or not
  //   Branch to subroutine
  //   Jump to targetted instruction
  //   Load value to mbr from memory location
  //   Halt the program execution
  //   Increment value to memory location
  //   Increment value of mbr by 1
  //   Perform bitwise left shift operation
  //   Perform bitwise right shift operation
  //   Add value with mbr with the targetted memory location
  //   Store value of mbr to desired location
  //   Calculate 2's complement of desired location value
endmodule
