// Logisim project INTERNAL-REGISTERS.circ as structural Verilog: 11 circuits, main circuit 1BIT-PLR
module _1BIT_PLR (
  input  LOAD,
  input  In,
  input  Clock,
  input  Clear,
  output Out
);

  wire and_1_out, and_2_out, not_1_out;

  not not_1 (not_1_out, In);
  and and_1 (and_1_out, not_1_out, LOAD);
  and and_2 (and_2_out, In, LOAD);
  J_K_Flip_Flop j_k_ff_1 (.J(and_2_out), .clk(Clock), .K(and_1_out), .Q(Out), .reset(Clear));  // open: Qn, preset, en
endmodule

module _4BIT_PLR (
  input  LOAD,
  input  [3:0] in_2,
  input  Clock,
  input  Clear,
  output [3:0] out_5
);

  wire and_1_out, and_2_out, and_3_out, and_4_out, and_5_out, and_6_out, and_7_out, and_8_out, not_1_out,
       not_2_out, not_3_out, not_4_out;

  not not_1 (not_1_out, in_2[0]);
  not not_2 (not_2_out, in_2[1]);
  not not_3 (not_3_out, in_2[2]);
  not not_4 (not_4_out, in_2[3]);
  and and_1 (and_1_out, in_2[0], LOAD);
  and and_2 (and_2_out, not_1_out, LOAD);
  and and_3 (and_3_out, in_2[1], LOAD);
  and and_4 (and_4_out, not_2_out, LOAD);
  and and_5 (and_5_out, in_2[2], LOAD);
  and and_6 (and_6_out, not_3_out, LOAD);
  and and_7 (and_7_out, in_2[3], LOAD);
  and and_8 (and_8_out, not_4_out, LOAD);
  J_K_Flip_Flop j_k_ff_1 (
    .J(and_1_out), .clk(Clock), .K(and_2_out), .Q(out_5[0]), .reset(Clear));  // open: Qn, preset, en
  J_K_Flip_Flop j_k_ff_2 (
    .J(and_5_out), .clk(Clock), .K(and_6_out), .Q(out_5[2]), .reset(Clear));  // open: Qn, preset, en
  J_K_Flip_Flop j_k_ff_3 (
    .J(and_3_out), .clk(Clock), .K(and_4_out), .Q(out_5[1]), .reset(Clear));  // open: Qn, preset, en
  J_K_Flip_Flop j_k_ff_4 (
    .J(and_7_out), .clk(Clock), .K(and_8_out), .Q(out_5[3]), .reset(Clear));  // open: Qn, preset, en
endmodule

// MBR
module _29BIT_PLR (
  input  Load,
  input  [28:0] Input,
  input  in_3,
  input  Clear,
  output [28:0] Output
);

  wire CLK_out;

  Clock CLK (.out(CLK_out));
  _4BIT_PLR u_4bit_plr_1 (.LOAD(Load), .in_2(Input[3:0]), .Clock(CLK_out), .Clear(Clear), .out_5(Output[3:0]));
  _4BIT_PLR u_4bit_plr_2 (.LOAD(Load), .in_2(Input[7:4]), .Clock(CLK_out), .Clear(Clear), .out_5(Output[7:4]));
  _4BIT_PLR u_4bit_plr_3 (.LOAD(Load), .in_2(Input[11:8]), .Clock(CLK_out), .Clear(Clear), .out_5(Output[11:8]));
  _4BIT_PLR u_4bit_plr_4 (.LOAD(Load), .in_2(Input[15:12]), .Clock(CLK_out), .Clear(Clear), .out_5(Output[15:12]));
  _4BIT_PLR u_4bit_plr_5 (.LOAD(Load), .in_2(Input[19:16]), .Clock(CLK_out), .Clear(Clear), .out_5(Output[19:16]));
  _4BIT_PLR u_4bit_plr_6 (.LOAD(Load), .in_2(Input[23:20]), .Clock(CLK_out), .Clear(Clear), .out_5(Output[23:20]));
  _4BIT_PLR u_4bit_plr_7 (.LOAD(Load), .in_2(Input[27:24]), .Clock(CLK_out), .Clear(Clear), .out_5(Output[27:24]));
  _1BIT_PLR u_1bit_plr_1 (.LOAD(Load), .In(Input[28]), .Clock(CLK_out), .Clear(Clear), .Out(Output[28]));
endmodule

module _1BIT_CPLR (
  input  Cin,
  input  Count,
  input  LOAD,
  input  In,
  input  Clear,
  input  CLK,
  output Out,
  output Cout
);

  wire and_1_out, and_2_out, and_3_out, and_4_out, not_1_out, not_2_out, or_1_out, or_2_out;

  not not_1 (not_1_out, LOAD);
  and and_1 (and_1_out, Count, not_1_out);
  not not_2 (not_2_out, In);
  and and_2 (and_2_out, LOAD, In);
  and and_3 (and_3_out, LOAD, not_2_out);
  and and_4 (and_4_out, and_1_out, Cin);
  or or_1 (or_1_out, and_2_out, and_4_out);
  or or_2 (or_2_out, and_4_out, and_3_out);
  J_K_Flip_Flop j_k_ff_1 (.J(or_1_out), .clk(CLK), .K(or_2_out), .Q(Out), .reset(Clear));  // open: Qn, preset, en
  and and_5 (Cout, Out, and_1_out, Cin);
endmodule

module _4BIT_CPLR (
  input  Cin,
  input  Count,
  input  Load,
  input  [3:0] In,
  input  Clock,
  input  Clear,
  output [3:0] Out,
  output Cout
);

  wire and_1_out, and_2_out, and_3_out, and_4_out, and_5_out, and_6_out, and_7_out, and_8_out, and_9_out,
       and_10_out, and_11_out, and_12_out, and_13_out, not_1_out, not_2_out, not_3_out, not_4_out, not_5_out,
       or_1_out, or_2_out, or_3_out, or_4_out, or_5_out, or_6_out, or_7_out, or_8_out;

  not not_1 (not_1_out, Load);
  and and_1 (and_1_out, Count, not_1_out);
  and and_2 (and_2_out, Load, In[0]);
  and and_3 (and_3_out, Load, not_2_out);
  not not_2 (not_2_out, In[0]);
  and and_4 (and_4_out, Load, In[1]);
  and and_5 (and_5_out, Load, not_3_out);
  not not_3 (not_3_out, In[1]);
  and and_6 (and_6_out, Load, In[2]);
  and and_7 (and_7_out, Load, not_4_out);
  not not_4 (not_4_out, In[2]);
  and and_8 (and_8_out, Load, In[3]);
  and and_9 (and_9_out, Load, not_5_out);
  not not_5 (not_5_out, In[3]);
  and and_10 (and_10_out, and_1_out, Cin);
  and and_11 (and_11_out, and_1_out, Cin, Out[0]);
  and and_12 (and_12_out, Out[0], Cin, Out[1], and_1_out);
  or or_1 (or_1_out, and_12_out, and_7_out);
  and and_13 (and_13_out, and_1_out, Out[0], Cin, Out[1], Out[2]);
  or or_2 (or_2_out, and_2_out, and_10_out);
  or or_3 (or_3_out, and_10_out, and_3_out);
  or or_4 (or_4_out, and_4_out, and_11_out);
  or or_5 (or_5_out, and_11_out, and_5_out);
  or or_6 (or_6_out, and_6_out, and_12_out);
  or or_7 (or_7_out, and_8_out, and_13_out);
  or or_8 (or_8_out, and_13_out, and_9_out);
  J_K_Flip_Flop j_k_ff_1 (.J(or_2_out), .clk(Clock), .K(or_3_out), .Q(Out[0]), .reset(Clear));  // open: Qn, preset, en
  J_K_Flip_Flop j_k_ff_2 (.J(or_4_out), .clk(Clock), .K(or_5_out), .Q(Out[1]), .reset(Clear));  // open: Qn, preset, en
  J_K_Flip_Flop j_k_ff_3 (.J(or_6_out), .clk(Clock), .K(or_1_out), .Q(Out[2]), .reset(Clear));  // open: Qn, preset, en
  J_K_Flip_Flop j_k_ff_4 (.J(or_7_out), .clk(Clock), .K(or_8_out), .Q(Out[3]), .reset(Clear));  // open: Qn, preset, en
  and and_14 (Cout, Out[2], Out[0], Out[1], Out[3], and_1_out, Cin);
  // Probe on Out
endmodule

// MBR
module _29BIT_CPLR (
  input  Load,
  input  Count,
  input  [28:0] In,
  input  clk,
  input  CLR,
  output [28:0] Out
);

  wire n4bit_cplr_1_cout, n4bit_cplr_2_cout, n4bit_cplr_3_cout, n4bit_cplr_4_cout, n4bit_cplr_5_cout,
       n4bit_cplr_6_cout, n4bit_cplr_7_cout;

  _4BIT_CPLR u_4bit_cplr_1 (
    .Cin(Count), .Count(Count), .Load(Load), .In(In[3:0]), .Clock(clk), .Clear(CLR), .Out(Out[3:0]),
    .Cout(n4bit_cplr_1_cout));
  _4BIT_CPLR u_4bit_cplr_2 (
    .Cin(n4bit_cplr_1_cout), .Count(Count), .Load(Load), .In(In[7:4]), .Clock(clk), .Clear(CLR),
    .Out(Out[7:4]), .Cout(n4bit_cplr_2_cout));
  _4BIT_CPLR u_4bit_cplr_3 (
    .Cin(n4bit_cplr_2_cout), .Count(Count), .Load(Load), .In(In[11:8]), .Clock(clk), .Clear(CLR),
    .Out(Out[11:8]), .Cout(n4bit_cplr_3_cout));
  _4BIT_CPLR u_4bit_cplr_4 (
    .Cin(n4bit_cplr_3_cout), .Count(Count), .Load(Load), .In(In[15:12]), .Clock(clk), .Clear(CLR),
    .Out(Out[15:12]), .Cout(n4bit_cplr_4_cout));
  _4BIT_CPLR u_4bit_cplr_5 (
    .Cin(n4bit_cplr_4_cout), .Count(Count), .Load(Load), .In(In[19:16]), .Clock(clk), .Clear(CLR),
    .Out(Out[19:16]), .Cout(n4bit_cplr_5_cout));
  _4BIT_CPLR u_4bit_cplr_6 (
    .Cin(n4bit_cplr_5_cout), .Count(Count), .Load(Load), .In(In[23:20]), .Clock(clk), .Clear(CLR),
    .Out(Out[23:20]), .Cout(n4bit_cplr_6_cout));
  _4BIT_CPLR u_4bit_cplr_7 (
    .Cin(n4bit_cplr_6_cout), .Count(Count), .Load(Load), .In(In[27:24]), .Clock(clk), .Clear(CLR),
    .Out(Out[27:24]), .Cout(n4bit_cplr_7_cout));
  _1BIT_CPLR u_1bit_cplr_1 (
    .Cin(n4bit_cplr_7_cout), .Count(Count), .LOAD(Load), .In(In[28]), .Clear(CLR), .CLK(clk), .Out(Out[28]));  // open: Cout
  // Probe on Out
endmodule

// IR
module _4BIT_IR (
  input  LOAD,
  input  [3:0] in_2,
  input  Clock,
  input  Clear,
  output [3:0] out_5
);

  wire and_1_out, and_2_out, and_3_out, and_4_out, and_5_out, and_6_out, and_7_out, and_8_out, not_1_out,
       not_2_out, not_3_out, not_4_out;

  not not_1 (not_1_out, in_2[0]);
  not not_2 (not_2_out, in_2[1]);
  not not_3 (not_3_out, in_2[2]);
  not not_4 (not_4_out, in_2[3]);
  and and_1 (and_1_out, in_2[0], LOAD);
  and and_2 (and_2_out, not_1_out, LOAD);
  and and_3 (and_3_out, in_2[1], LOAD);
  and and_4 (and_4_out, not_2_out, LOAD);
  and and_5 (and_5_out, in_2[2], LOAD);
  and and_6 (and_6_out, not_3_out, LOAD);
  and and_7 (and_7_out, in_2[3], LOAD);
  and and_8 (and_8_out, not_4_out, LOAD);
  J_K_Flip_Flop j_k_ff_1 (
    .J(and_3_out), .clk(Clock), .K(and_4_out), .Q(out_5[1]), .reset(Clear));  // open: Qn, preset, en
  J_K_Flip_Flop j_k_ff_2 (
    .J(and_5_out), .clk(Clock), .K(and_6_out), .Q(out_5[2]), .reset(Clear));  // open: Qn, preset, en
  J_K_Flip_Flop j_k_ff_3 (
    .J(and_1_out), .clk(Clock), .K(and_2_out), .Q(out_5[0]), .reset(Clear));  // open: Qn, preset, en
  J_K_Flip_Flop j_k_ff_4 (
    .J(and_7_out), .clk(Clock), .K(and_8_out), .Q(out_5[3]), .reset(Clear));  // open: Qn, preset, en
endmodule

// MAR
module _5BIT_MAR (
  input  Load,
  input  [4:0] In,
  input  in_3,
  input  Clear,
  output [4:0] Out
);

  wire Clock_out;

  Clock Clock (.out(Clock_out));
  _4BIT_PLR u_4bit_plr_1 (.LOAD(Load), .in_2(In[3:0]), .Clock(Clock_out), .Clear(Clear), .out_5(Out[3:0]));
  _1BIT_PLR u_1bit_plr_1 (.LOAD(Load), .In(In[4]), .Clock(Clock_out), .Clear(Clear), .Out(Out[4]));
endmodule

// PC
module _5BIT_PC (
  input  Load,
  input  Count,
  input  [4:0] In,
  input  in_4,
  input  CLEAR,
  output [4:0] out_6
);

  wire Clock_out, n4bit_cplr_1_cout;

  Clock Clock (.out(Clock_out));
  _4BIT_CPLR u_4bit_cplr_1 (
    .Cin(Count), .Count(Count), .Load(Load), .In(In[3:0]), .Clock(Clock_out), .Clear(CLEAR),
    .Out(out_6[3:0]), .Cout(n4bit_cplr_1_cout));
  _1BIT_CPLR u_1bit_cplr_1 (
    .Cin(n4bit_cplr_1_cout), .Count(Count), .LOAD(Load), .In(In[4]), .Clear(CLEAR), .CLK(Clock_out),
    .Out(out_6[4]));  // open: Cout
  // Probe on out_6
endmodule

// AC
module _29BIT_AC (
  input  Load,
  input  [28:0] Input,
  input  in_3,
  input  Clear,
  output [28:0] Output
);

  wire CLK_out;

  Clock CLK (.out(CLK_out));
  _4BIT_PLR u_4bit_plr_1 (.LOAD(Load), .in_2(Input[3:0]), .Clock(CLK_out), .Clear(Clear), .out_5(Output[3:0]));
  _4BIT_PLR u_4bit_plr_2 (.LOAD(Load), .in_2(Input[7:4]), .Clock(CLK_out), .Clear(Clear), .out_5(Output[7:4]));
  _4BIT_PLR u_4bit_plr_3 (.LOAD(Load), .in_2(Input[11:8]), .Clock(CLK_out), .Clear(Clear), .out_5(Output[11:8]));
  _4BIT_PLR u_4bit_plr_4 (.LOAD(Load), .in_2(Input[15:12]), .Clock(CLK_out), .Clear(Clear), .out_5(Output[15:12]));
  _4BIT_PLR u_4bit_plr_5 (.LOAD(Load), .in_2(Input[19:16]), .Clock(CLK_out), .Clear(Clear), .out_5(Output[19:16]));
  _4BIT_PLR u_4bit_plr_6 (.LOAD(Load), .in_2(Input[23:20]), .Clock(CLK_out), .Clear(Clear), .out_5(Output[23:20]));
  _4BIT_PLR u_4bit_plr_7 (.LOAD(Load), .in_2(Input[27:24]), .Clock(CLK_out), .Clear(Clear), .out_5(Output[27:24]));
  _1BIT_PLR u_1bit_plr_1 (.LOAD(Load), .In(Input[28]), .Clock(CLK_out), .Clear(Clear), .Out(Output[28]));
endmodule

module REGISTERS (
  input  Load,
  input  Count,
  input  [3:0] IRin,
  input  [28:0] MBRACin,
  input  [4:0] MARPCin,
  input  Reset,
  output [28:0] MBRout,
  output [3:0] IRout,
  output [28:0] ACout,
  output [4:0] MARout,
  output [4:0] PCout
);

  wire clock_1_out;

  Clock clock_1 (.out(clock_1_out));
  // Probe on MBRout
  _29BIT_CPLR u_29bit_cplr_1 (.Count(Count), .In(MBRACin), .CLR(Reset), .Out(MBRout), .Load(Load), .clk(clock_1_out));
  _4BIT_IR u_4bit_ir_1 (.LOAD(Load), .in_2(IRin), .Clock(clock_1_out), .Clear(Reset), .out_5(IRout));
  _5BIT_MAR u_5bit_mar_1 (.In(MARPCin), .in_3(clock_1_out), .Clear(Reset), .Load(Load), .Out(MARout));
  _29BIT_AC u_29bit_ac_1 (.Input(MBRACin), .in_3(clock_1_out), .Clear(Reset), .Load(Load), .Output(ACout));
  // Probe on PCout
  _5BIT_PC u_5bit_pc_1 (.Count(Count), .In(MARPCin), .in_4(clock_1_out), .CLEAR(Reset), .Load(Load), .out_6(PCout));
endmodule
